// Logisim project 7 seg.circ as structural Verilog: 1 circuit, main circuit main
module main (
  input  A,
  input  B,
  input  C,
  input  D
);

  wire a_out, b_out, B_prime_C_out, B_prime_D_prime_out, BC_prime_D_out, BC_prime_out, BD_out, BD_prime_out,
       c_out, C_prime_D_prime_out, CD_out, CD_prime_out, d_out, e_out, f_out, g_out, not_1_out;

  and BD (BD_out, B, D);
  and B_prime_D_prime (B_prime_D_prime_out, ~B, ~D);  // AND_Gate
  and CD (CD_out, D, C);
  and C_prime_D_prime (C_prime_D_prime_out, ~C, ~D);  // AND_Gate
  and CD_prime (CD_prime_out, C, ~D);  // AND_Gate
  and BC_prime_D (BC_prime_D_out, B, ~C, D);  // AND_Gate
  not not_1 (not_1_out, C);
  and BD_prime (BD_prime_out, B, ~D);  // AND_Gate
  and BC_prime (BC_prime_out, B, ~C);  // AND_Gate
  and B_prime_C (B_prime_C_out, C, ~B);  // AND_Gate
  or u_c (c_out, D, not_1_out, B);
  or u_a (a_out, C, A, BD_out, B_prime_D_prime_out);
  or u_b (b_out, ~B, CD_out, C_prime_D_prime_out);  // OR_Gate
  or u_d (d_out, B_prime_D_prime_out, A, B_prime_C_out, CD_prime_out, BC_prime_D_out);
  or f (f_out, C_prime_D_prime_out, A, BD_prime_out, BC_prime_out);
  or g (g_out, BC_prime_out, A, CD_prime_out, B_prime_C_out);
  or e (e_out, B_prime_D_prime_out, CD_prime_out);
  _7_Segment_Display u_7_segment_display_1 (
    .g(g_out), .f(f_out), .a(a_out), .b(b_out), .e(e_out), .d(d_out), .c(c_out));  // open: dp
endmodule
