// Logisim project Retry.circ as structural Verilog: 5 circuits, main circuit main
module main (
  input  A_7,
  input  A_6,
  input  A_5,
  input  A_4,
  input  A_3,
  input  A_2,
  input  A_1,
  input  A_0,
  input  in_9,
  input  R,
  input  in_11
);

  wire and_1_out, and_2_out, and_3_out, and_4_out, and_5_out, and_6_out, and_7_out, and_8_out, CLK_out,
       csa_1_sum, csa_2_sum, csa_3_sum, csa_4_sum, csa_5_sum, csa_6_sum, csa_7_sum, multiplexer_1_out,
       multiplexer_2_out, n2s_complement_1_s, n8_counter_1_led, n8_counter_1_mux, not_1_out,
       shift_register_1_out, shift_register_1_q0;

  Multiplexer multiplexer_1 (.in0(1'b0), .in1(1'b1), .out(multiplexer_1_out), .sel(shift_register_1_q0));  // open: en
  Multiplexer multiplexer_2 (
    .in0(multiplexer_1_out), .in1(in_9), .out(multiplexer_2_out), .sel(n8_counter_1_mux));  // open: en
  Clock CLK (.out(CLK_out));
  Shift_Register shift_register_1 (
    .in(multiplexer_2_out), .clk(CLK_out), .out(shift_register_1_out), .clr(R), .q0(shift_register_1_q0));  // open: shift, load, d0, d1, q1, d2, q2, d3, q3, d4, q4, d5, q5, d6, q6, d7, q7
  LED led_1 (.in(n8_counter_1_led));
  _8_Counter u_8_counter_1 (.CLK(CLK_out), .R(R), .LED(n8_counter_1_led), .MUX(n8_counter_1_mux));
  and and_1 (and_1_out, shift_register_1_out, A_7);
  and and_2 (and_2_out, shift_register_1_out, A_6);
  _2s_Complement u_2s_complement_1 (.A(and_1_out), .CLK(CLK_out), .R(R), .S(n2s_complement_1_s));  // open: FDHA
  and and_3 (and_3_out, shift_register_1_out, A_5);
  CSA csa_1 (.X(and_2_out), .Y(n2s_complement_1_s), .CLK(CLK_out), .R(R), .SUM(csa_1_sum));  // open: FDHA
  CSA csa_2 (.X(and_3_out), .Y(csa_1_sum), .CLK(CLK_out), .R(R), .SUM(csa_2_sum));  // open: FDHA
  and and_4 (and_4_out, shift_register_1_out, A_4);
  CSA csa_3 (.X(and_4_out), .Y(csa_2_sum), .CLK(CLK_out), .R(R), .SUM(csa_3_sum));  // open: FDHA
  and and_5 (and_5_out, shift_register_1_out, A_3);
  CSA csa_4 (.X(and_5_out), .Y(csa_3_sum), .CLK(CLK_out), .R(R), .SUM(csa_4_sum));  // open: FDHA
  and and_6 (and_6_out, shift_register_1_out, A_2);
  CSA csa_5 (.X(and_6_out), .Y(csa_4_sum), .CLK(CLK_out), .R(R), .SUM(csa_5_sum));  // open: FDHA
  and and_7 (and_7_out, shift_register_1_out, A_1);
  and and_8 (and_8_out, shift_register_1_out, A_0);
  CSA csa_6 (.X(and_7_out), .Y(csa_5_sum), .CLK(CLK_out), .R(R), .SUM(csa_6_sum));  // open: FDHA
  not not_1 (not_1_out, in_11);
  CSA csa_7 (.X(and_8_out), .Y(csa_6_sum), .CLK(CLK_out), .R(R), .SUM(csa_7_sum));  // open: FDHA
  _17_Counter u_17_counter_1 (.CLK(CLK_out), .R(R), .A(n8_counter_1_led));  // open: OUT
  LED led_2 (.in(not_1_out));
  Shift_Register #(.length(16)) shift_register_2 (
    .shift(in_11), .in(csa_7_sum), .clk(CLK_out), .clr(R));  // open: out, load, d0, q0, d1, q1, d2, q2, d3, q3, d4, q4, d5, q5, d6, q6, d7, q7, d8, q8, d9, q9, d10, q10, d11, q11, d12, q12, d13, q13, d14, q14, d15, q15
endmodule

module CSA (
  input  X,
  input  Y,
  input  CLK,
  input  R,
  output SUM,
  output FDHA
);

  wire adder_1_cout, adder_1_out, and_1_out, d_ff_2_q, xor_1_out, xor_2_out;

  and and_1 (and_1_out, X, adder_1_out);
  xor xor_1 (xor_1_out, X, adder_1_out);
  Adder #(.width(1)) adder_1 (.a(Y), .b(d_ff_2_q), .out(adder_1_out), .cout(adder_1_cout));  // open: cin
  D_Flip_Flop d_ff_1 (.clk(CLK), .D(xor_1_out), .Q(SUM), .reset(R));  // open: Qn, preset, en
  and and_2 (FDHA, and_1_out, adder_1_cout);
  xor xor_2 (xor_2_out, and_1_out, adder_1_cout);
  D_Flip_Flop d_ff_2 (.clk(CLK), .D(xor_2_out), .Q(d_ff_2_q), .reset(R));  // open: Qn, preset, en
endmodule

module _2s_Complement (
  input  A,
  input  CLK,
  input  R,
  output FDHA,
  output S
);

  wire d_ff_2_q, or_1_out, xor_1_out;

  and and_1 (FDHA, A, d_ff_2_q);
  D_Flip_Flop d_ff_1 (.clk(CLK), .D(xor_1_out), .Q(S), .reset(R));  // open: Qn, preset, en
  xor xor_1 (xor_1_out, A, d_ff_2_q);
  D_Flip_Flop d_ff_2 (.clk(CLK), .D(or_1_out), .Q(d_ff_2_q), .reset(R));  // open: Qn, preset, en
  or or_1 (or_1_out, A, d_ff_2_q);
endmodule

module _8_Counter (
  input  CLK,
  input  R,
  output LED,
  output MUX
);

  wire and_1_out, and_2_out, not_1_out, t_ff_1_q, t_ff_2_q, t_ff_3_q;

  T_Flip_Flop t_ff_1 (.clk(CLK), .T(not_1_out), .Q(t_ff_1_q), .reset(R), .en(MUX));  // open: Qn, preset
  not not_1 (not_1_out, R);
  and and_1 (and_1_out, t_ff_1_q, t_ff_2_q);
  T_Flip_Flop t_ff_2 (.clk(CLK), .T(t_ff_1_q), .Q(t_ff_2_q), .reset(R), .en(MUX));  // open: Qn, preset
  T_Flip_Flop t_ff_3 (.clk(CLK), .T(and_1_out), .Q(t_ff_3_q), .reset(R), .en(MUX));  // open: Qn, preset
  and and_2 (and_2_out, and_1_out, t_ff_3_q);
  T_Flip_Flop t_ff_4 (.clk(CLK), .T(and_2_out), .Q(LED), .reset(R), .en(MUX));  // open: Qn, preset
  not not_2 (MUX, LED);
endmodule

module _17_Counter (
  input  CLK,
  input  R,
  input  A,
  output OUT
);

  wire and_1_out, and_2_out, and_3_out, and_4_out, and_5_out, t_ff_1_q, t_ff_2_q, t_ff_3_q, t_ff_4_q,
       t_ff_5_q;

  and and_1 (and_1_out, R, A);
  T_Flip_Flop t_ff_1 (.clk(CLK), .T(and_1_out), .Q(t_ff_1_q), .preset(OUT), .reset(R), .en(OUT));  // open: Qn
  and and_2 (and_2_out, t_ff_1_q, t_ff_2_q);
  T_Flip_Flop t_ff_2 (.clk(CLK), .T(t_ff_1_q), .Q(t_ff_2_q), .reset(R), .en(OUT));  // open: Qn, preset
  T_Flip_Flop t_ff_3 (.clk(CLK), .T(and_2_out), .Q(t_ff_3_q), .reset(R), .en(OUT));  // open: Qn, preset
  and and_3 (and_3_out, and_2_out, t_ff_3_q);
  and and_4 (and_4_out, and_3_out, t_ff_4_q);
  T_Flip_Flop t_ff_4 (.clk(CLK), .T(and_3_out), .Q(t_ff_4_q), .reset(R), .en(OUT));  // open: Qn, preset
  T_Flip_Flop t_ff_5 (.clk(CLK), .T(and_4_out), .Q(t_ff_5_q), .reset(R), .en(OUT));  // open: Qn, preset
  and and_5 (and_5_out, t_ff_1_q, t_ff_5_q);
  not not_1 (OUT, and_5_out);
endmodule
