// Logisim project SPM.circ as structural Verilog: 1 circuit, main circuit main
module main (
  input  A_3,
  input  A_3_2,
  input  A_3_3,
  input  A_3_4,
  input  A_3_5,
  input  A_2,
  input  A_1,
  input  A_0,
  input  in_9,
  input  RST
);

  wire adder_1_cout, adder_1_out, adder_2_cout, adder_2_out, adder_3_cout, adder_3_out, adder_4_cout,
       adder_4_out, adder_5_cout, adder_5_out, adder_6_cout, adder_6_out, adder_7_cout, adder_7_out,
       and_1_out, and_2_out, and_3_out, and_4_out, and_5_out, and_6_out, and_7_out, and_8_out, and_9_out,
       and_10_out, and_11_out, and_12_out, and_13_out, and_14_out, and_15_out, and_16_out, and_17_out,
       and_18_out, and_19_out, and_20_out, and_21_out, and_22_out, B_out, B_q0, CLK_out, d_ff_1_q, d_ff_2_q,
       d_ff_3_q, d_ff_4_q, d_ff_5_q, d_ff_6_q, d_ff_7_q, d_ff_8_q, d_ff_9_q, d_ff_10_q, d_ff_11_q, d_ff_12_q,
       d_ff_13_q, d_ff_14_q, d_ff_15_q, d_ff_16_q, multiplexer_1_out, multiplexer_2_out, not_1_out,
       not_2_out, not_3_out, not_4_out, or_1_out, t_ff_1_q, t_ff_2_q, t_ff_3_q, t_ff_4_q, t_ff_5_q, t_ff_6_q,
       t_ff_7_q, t_ff_8_q, t_ff_9_q, xor_1_out, xor_2_out, xor_3_out, xor_4_out, xor_5_out, xor_6_out,
       xor_7_out, xor_8_out, xor_9_out, xor_10_out, xor_11_out, xor_12_out, xor_13_out, xor_14_out,
       xor_15_out;

  Multiplexer multiplexer_1 (.in0(1'b0), .in1(1'b1), .out(multiplexer_1_out), .sel(B_q0));  // open: en
  Clock CLK (.out(CLK_out));
  Shift_Register B (
    .in(multiplexer_2_out), .clk(CLK_out), .out(B_out), .clr(RST), .q0(B_q0));  // open: shift, load, d0, d1, q1, d2, q2, d3, q3, d4, q4, d5, q5, d6, q6, d7, q7
  Multiplexer multiplexer_2 (
    .in0(multiplexer_1_out), .in1(in_9), .out(multiplexer_2_out), .sel(not_2_out));  // open: en
  and and_1 (and_1_out, B_out, A_3_2);
  not not_1 (not_1_out, RST);
  xor xor_1 (xor_1_out, and_1_out, d_ff_1_q);
  D_Flip_Flop #(.trigger("high")) d_ff_1 (
    .clk(CLK_out), .D(or_1_out), .Q(d_ff_1_q), .reset(RST));  // open: Qn, preset, en
  or or_1 (or_1_out, and_1_out, d_ff_1_q);
  T_Flip_Flop t_ff_1 (.clk(CLK_out), .T(not_1_out), .Q(t_ff_1_q), .reset(RST), .en(not_2_out));  // open: Qn, preset
  D_Flip_Flop #(.trigger("high")) d_ff_2 (
    .clk(CLK_out), .D(xor_1_out), .Q(d_ff_2_q), .reset(RST));  // open: Qn, preset, en
  and and_2 (and_2_out, t_ff_1_q, t_ff_2_q);
  T_Flip_Flop t_ff_2 (.clk(CLK_out), .T(t_ff_1_q), .Q(t_ff_2_q), .reset(RST), .en(not_2_out));  // open: Qn, preset
  and and_3 (and_3_out, B_out, A_3);
  T_Flip_Flop t_ff_3 (.clk(CLK_out), .T(and_2_out), .Q(t_ff_3_q), .reset(RST), .en(not_2_out));  // open: Qn, preset
  and and_4 (and_4_out, adder_1_out, and_3_out);
  xor xor_2 (xor_2_out, and_3_out, adder_1_out);
  Adder #(.width(1)) adder_1 (.a(d_ff_2_q), .b(d_ff_3_q), .out(adder_1_out), .cout(adder_1_cout));  // open: cin
  and and_5 (and_5_out, and_2_out, t_ff_3_q);
  T_Flip_Flop t_ff_4 (.clk(CLK_out), .T(and_5_out), .Q(t_ff_4_q), .reset(RST), .en(not_2_out));  // open: Qn, preset
  xor xor_3 (xor_3_out, and_4_out, adder_1_cout);
  LED led_1 (.in(t_ff_4_q));
  not not_2 (not_2_out, t_ff_4_q);
  D_Flip_Flop d_ff_3 (.clk(CLK_out), .D(xor_3_out), .Q(d_ff_3_q), .reset(RST));  // open: Qn, preset, en
  and and_6 (and_6_out, B_out, A_3_3);
  D_Flip_Flop d_ff_4 (.clk(CLK_out), .D(xor_2_out), .Q(d_ff_4_q), .reset(RST));  // open: Qn, preset, en
  and and_7 (and_7_out, adder_2_out, and_6_out);
  xor xor_4 (xor_4_out, and_6_out, adder_2_out);
  Adder #(.width(1)) adder_2 (.a(d_ff_4_q), .b(d_ff_6_q), .out(adder_2_out), .cout(adder_2_cout));  // open: cin
  xor xor_5 (xor_5_out, and_7_out, adder_2_cout);
  D_Flip_Flop d_ff_5 (.clk(CLK_out), .D(xor_4_out), .Q(d_ff_5_q), .reset(RST));  // open: Qn, preset, en
  D_Flip_Flop d_ff_6 (.clk(CLK_out), .D(xor_5_out), .Q(d_ff_6_q), .reset(RST));  // open: Qn, preset, en
  and and_8 (and_8_out, B_out, A_3_4);
  and and_9 (and_9_out, adder_3_out, and_8_out);
  xor xor_6 (xor_6_out, and_8_out, adder_3_out);
  Adder #(.width(1)) adder_3 (.a(d_ff_5_q), .b(d_ff_8_q), .out(adder_3_out), .cout(adder_3_cout));  // open: cin
  xor xor_7 (xor_7_out, and_9_out, adder_3_cout);
  D_Flip_Flop d_ff_7 (.clk(CLK_out), .D(xor_6_out), .Q(d_ff_7_q), .reset(RST));  // open: Qn, preset, en
  D_Flip_Flop d_ff_8 (.clk(CLK_out), .D(xor_7_out), .Q(d_ff_8_q), .reset(RST));  // open: Qn, preset, en
  and and_10 (and_10_out, B_out, A_3_5);
  and and_11 (and_11_out, t_ff_4_q, ~RST);  // AND_Gate
  and and_12 (and_12_out, adder_4_out, and_10_out);
  xor xor_8 (xor_8_out, and_10_out, adder_4_out);
  Adder #(.width(1)) adder_4 (.a(d_ff_7_q), .b(d_ff_9_q), .out(adder_4_out), .cout(adder_4_cout));  // open: cin
  T_Flip_Flop t_ff_5 (.clk(CLK_out), .T(and_11_out), .Q(t_ff_5_q), .reset(RST), .en(not_3_out));  // open: Qn, preset
  and and_13 (and_13_out, t_ff_5_q, t_ff_6_q);
  T_Flip_Flop t_ff_6 (.clk(CLK_out), .T(t_ff_5_q), .Q(t_ff_6_q), .reset(RST), .en(not_3_out));  // open: Qn, preset
  D_Flip_Flop d_ff_9 (.clk(CLK_out), .D(xor_9_out), .Q(d_ff_9_q), .reset(RST));  // open: Qn, preset, en
  xor xor_9 (xor_9_out, and_12_out, adder_4_cout);
  T_Flip_Flop t_ff_7 (.clk(CLK_out), .T(and_13_out), .Q(t_ff_7_q), .reset(RST), .en(not_3_out));  // open: Qn, preset
  D_Flip_Flop d_ff_10 (.clk(CLK_out), .D(xor_8_out), .Q(d_ff_10_q), .reset(RST));  // open: Qn, preset, en
  and and_14 (and_14_out, and_13_out, t_ff_7_q);
  and and_15 (and_15_out, B_out, A_2);
  T_Flip_Flop t_ff_8 (.clk(CLK_out), .T(and_14_out), .Q(t_ff_8_q), .reset(RST), .en(not_3_out));  // open: Qn, preset
  and and_16 (and_16_out, adder_5_out, and_15_out);
  xor xor_10 (xor_10_out, and_15_out, adder_5_out);
  Adder #(.width(1)) adder_5 (.a(d_ff_10_q), .b(d_ff_11_q), .out(adder_5_out), .cout(adder_5_cout));  // open: cin
  and and_17 (and_17_out, and_14_out, t_ff_8_q);
  xor xor_11 (xor_11_out, and_16_out, adder_5_cout);
  T_Flip_Flop t_ff_9 (.clk(CLK_out), .T(and_17_out), .Q(t_ff_9_q), .reset(RST), .en(not_3_out));  // open: Qn, preset
  D_Flip_Flop d_ff_11 (.clk(CLK_out), .D(xor_11_out), .Q(d_ff_11_q), .reset(RST));  // open: Qn, preset, en
  and and_18 (and_18_out, t_ff_9_q, t_ff_5_q);
  and and_19 (and_19_out, B_out, A_1);
  D_Flip_Flop d_ff_12 (.clk(CLK_out), .D(xor_10_out), .Q(d_ff_12_q), .reset(RST));  // open: Qn, preset, en
  not not_3 (not_3_out, and_18_out);
  and and_20 (and_20_out, adder_6_out, and_19_out);
  xor xor_12 (xor_12_out, and_19_out, adder_6_out);
  Adder #(.width(1)) adder_6 (.a(d_ff_12_q), .b(d_ff_14_q), .out(adder_6_out), .cout(adder_6_cout));  // open: cin
  xor xor_13 (xor_13_out, and_20_out, adder_6_cout);
  D_Flip_Flop d_ff_13 (.clk(CLK_out), .D(xor_12_out), .Q(d_ff_13_q), .reset(RST));  // open: Qn, preset, en
  D_Flip_Flop d_ff_14 (.clk(CLK_out), .D(xor_13_out), .Q(d_ff_14_q), .reset(RST));  // open: Qn, preset, en
  and and_21 (and_21_out, B_out, A_0);
  and and_22 (and_22_out, adder_7_out, and_21_out);
  xor xor_14 (xor_14_out, and_21_out, adder_7_out);
  Adder #(.width(1)) adder_7 (.a(d_ff_13_q), .b(d_ff_16_q), .out(adder_7_out), .cout(adder_7_cout));  // open: cin
  xor xor_15 (xor_15_out, and_22_out, adder_7_cout);
  D_Flip_Flop d_ff_15 (.clk(CLK_out), .D(xor_14_out), .Q(d_ff_15_q), .reset(RST));  // open: Qn, preset, en
  D_Flip_Flop d_ff_16 (.clk(CLK_out), .D(xor_15_out), .Q(d_ff_16_q), .reset(RST));  // open: Qn, preset, en
  LED led_2 (.in(not_4_out));
  not not_4 (not_4_out, not_3_out);
  Shift_Register #(.length(16)) shift_register_1 (
    .shift(not_3_out), .in(d_ff_15_q), .clk(CLK_out), .clr(RST));  // open: out, load, d0, q0, d1, q1, d2, q2, d3, q3, d4, q4, d5, q5, d6, q6, d7, q7, d8, q8, d9, q9, d10, q10, d11, q11, d12, q12, d13, q13, d14, q14, d15, q15
endmodule
