// Logisim project updated 7 seg.circ as structural Verilog: 7 circuits, main circuit 8bitDD
module main (
  input  A,
  input  B,
  input  C,
  input  D,
  output out_5,
  output out_6,
  output out_7,
  output out_8,
  output out_9,
  output out_10,
  output out_11
);

  wire B_prime_C_out, B_prime_D_prime_out, BC_prime_D_out, BC_prime_out, BD_out, BD_prime_out,
       C_prime_D_prime_out, CD_out, CD_prime_out, not_1_out;

  and BD (BD_out, B, D);
  and B_prime_D_prime (B_prime_D_prime_out, ~B, ~D);  // AND_Gate
  and CD (CD_out, D, C);
  and C_prime_D_prime (C_prime_D_prime_out, ~C, ~D);  // AND_Gate
  and CD_prime (CD_prime_out, C, ~D);  // AND_Gate
  and BC_prime_D (BC_prime_D_out, B, ~C, D);  // AND_Gate
  not not_1 (not_1_out, C);
  and BD_prime (BD_prime_out, B, ~D);  // AND_Gate
  and BC_prime (BC_prime_out, B, ~C);  // AND_Gate
  and B_prime_C (B_prime_C_out, C, ~B);  // AND_Gate
  or u_c (out_11, D, not_1_out, B);
  or u_a (out_5, C, A, BD_out, B_prime_D_prime_out);
  or u_b (out_6, ~B, CD_out, C_prime_D_prime_out);  // OR_Gate
  or u_d (out_10, B_prime_D_prime_out, A, B_prime_C_out, CD_prime_out, BC_prime_D_out);
  or f (out_7, C_prime_D_prime_out, A, BD_prime_out, BC_prime_out);
  or g (out_8, BC_prime_out, A, CD_prime_out, B_prime_C_out);
  or e (out_9, B_prime_D_prime_out, CD_prime_out);
endmodule

module CompAdder (
  input  in_1,
  input  in_2,
  input  in_3,
  input  in_4,
  output out_5,
  output out_6,
  output out_7,
  output out_8
);

  wire n4comp_1_out_5;
  wire [1:0] n4bitadder_1_out_5;
  wire [3:2] n4bitadder_1_out_7;

  _4bitAdder u_4bitadder_1 (
    .in_1(in_1), .in_2(in_2), .in_3(in_3), .in_4(in_4), .out_5(n4bitadder_1_out_5[0]),
    .out_6(n4bitadder_1_out_5[1]), .out_7(n4bitadder_1_out_7[2]), .out_8(n4bitadder_1_out_7[3]));
  _4comp u_4comp_1 (.in_1(in_4), .in_2(in_3), .in_3(in_2), .in_4(in_1), .out_5(n4comp_1_out_5));
  Multiplexer #(.width(4)) multiplexer_1 (
    .in0({in_4, in_3, in_2, in_1}), .in1({n4bitadder_1_out_7, n4bitadder_1_out_5}),
    .out({out_8, out_7, out_6, out_5}), .sel(n4comp_1_out_5));  // open: en
endmodule

module _4bitAdder (
  input  in_1,
  input  in_2,
  input  in_3,
  input  in_4,
  output out_5,
  output out_6,
  output out_7,
  output out_8
);

  wire and_1_out, and_2_out, and_3_out, and_4_out, and_5_out, or_1_out, or_2_out, xor_1_out, xor_3_out,
       xor_4_out;

  xor xor_1 (xor_1_out, 1'b0, in_4);
  xor xor_2 (out_5, 1'b1, in_1);
  and and_1 (and_1_out, 1'b1, in_1);
  xor xor_3 (xor_3_out, 1'b1, in_2);
  and and_2 (and_2_out, 1'b1, in_2);
  xor xor_4 (xor_4_out, 1'b0, in_3);
  and and_3 (and_3_out, 1'b0, in_3);
  xor xor_5 (out_6, and_1_out, xor_3_out);
  and and_4 (and_4_out, xor_3_out, and_1_out);
  or or_1 (or_1_out, and_4_out, and_2_out);
  and and_5 (and_5_out, or_1_out, xor_4_out);
  xor xor_6 (out_7, or_1_out, xor_4_out);
  or or_2 (or_2_out, and_5_out, and_3_out);
  xor xor_7 (out_8, or_2_out, xor_1_out);
endmodule

module _4comp (
  input  in_1,
  input  in_2,
  input  in_3,
  input  in_4,
  output out_5
);

  wire and_1_out, and_2_out, and_3_out, and_4_out, xnor_1_out, xnor_2_out, xnor_3_out;

  and and_1 (and_1_out, ~1'b0, in_1);  // AND_Gate
  xnor xnor_1 (xnor_1_out, 1'b0, in_1);
  xnor xnor_2 (xnor_2_out, 1'b1, in_2);
  xnor xnor_3 (xnor_3_out, 1'b0, in_3);
  and and_2 (and_2_out, xnor_1_out, ~1'b1, in_2);  // AND_Gate
  and and_3 (and_3_out, xnor_1_out, xnor_2_out, ~1'b0, in_3);  // AND_Gate
  and and_4 (and_4_out, xnor_1_out, xnor_2_out, xnor_3_out, ~1'b0, in_4);  // AND_Gate
  or or_1 (out_5, and_1_out, and_2_out, and_3_out, and_4_out);
endmodule

module _8bitDD (
  input  in_1,
  input  in_2,
  input  in_3,
  input  in_4,
  input  in_5,
  input  in_6,
  input  in_7,
  input  in_8,
  output [3:0] out_9,
  output [3:0] out_10,
  output [3:0] out_11
);

  wire compadder_1_out_5, compadder_1_out_6, compadder_1_out_7, compadder_1_out_8, compadder_2_out_5,
       compadder_2_out_6, compadder_2_out_7, compadder_2_out_8, compadder_3_out_5, compadder_3_out_6,
       compadder_3_out_7, compadder_3_out_8, compadder_4_out_5, compadder_4_out_6, compadder_4_out_7,
       compadder_4_out_8, compadder_5_out_5, compadder_5_out_6, compadder_5_out_7;

  CompAdder compadder_1 (
    .in_1(in_6), .in_2(in_7), .in_3(in_8), .in_4(1'b0), .out_5(compadder_1_out_5), .out_6(compadder_1_out_6),
    .out_7(compadder_1_out_7), .out_8(compadder_1_out_8));
  CompAdder compadder_2 (
    .in_1(in_4), .in_2(compadder_3_out_5), .in_3(compadder_3_out_6), .in_4(compadder_3_out_7),
    .out_5(compadder_2_out_5), .out_6(compadder_2_out_6), .out_7(compadder_2_out_7), .out_8(compadder_2_out_8));
  CompAdder compadder_3 (
    .in_1(in_5), .in_2(compadder_1_out_5), .in_3(compadder_1_out_6), .in_4(compadder_1_out_7),
    .out_5(compadder_3_out_5), .out_6(compadder_3_out_6), .out_7(compadder_3_out_7), .out_8(compadder_3_out_8));
  CompAdder compadder_4 (
    .in_1(in_3), .in_2(compadder_2_out_5), .in_3(compadder_2_out_6), .in_4(compadder_2_out_7),
    .out_5(compadder_4_out_5), .out_6(compadder_4_out_6), .out_7(compadder_4_out_7), .out_8(compadder_4_out_8));
  CompAdder compadder_5 (
    .in_1(compadder_2_out_8), .in_2(compadder_3_out_8), .in_3(compadder_1_out_8), .in_4(1'b0),
    .out_5(compadder_5_out_5), .out_6(compadder_5_out_6), .out_7(compadder_5_out_7), .out_8(out_11[1]));
  CompAdder compadder_6 (
    .in_1(in_2), .in_2(compadder_4_out_5), .in_3(compadder_4_out_6), .in_4(compadder_4_out_7),
    .out_5(out_9[1]), .out_6(out_9[2]), .out_7(out_9[3]), .out_8(out_10[0]));
  CompAdder compadder_7 (
    .in_1(compadder_4_out_8), .in_2(compadder_5_out_5), .in_3(compadder_5_out_6), .in_4(compadder_5_out_7),
    .out_5(out_10[1]), .out_6(out_10[2]), .out_7(out_10[3]), .out_8(out_11[0]));

  assign out_9[0] = in_1;
  assign out_11[3:2] = 2'b00;
endmodule

module Final_Display (
  input  [7:0] in_1
);

  wire main_1_out_5, main_1_out_6, main_1_out_7, main_1_out_8, main_1_out_9, main_1_out_10, main_1_out_11,
       main_2_out_5, main_2_out_6, main_2_out_7, main_2_out_8, main_2_out_9, main_2_out_10, main_2_out_11,
       main_3_out_5, main_3_out_6, main_3_out_7, main_3_out_8, main_3_out_9, main_3_out_10, main_3_out_11;
  wire [3:0] n8bitdd_1_out_9, n8bitdd_1_out_10, n8bitdd_1_out_11;

  _8bitDD u_8bitdd_1 (
    .in_1(in_1[0]), .in_2(in_1[1]), .in_3(in_1[2]), .in_4(in_1[3]), .in_5(in_1[4]), .in_6(in_1[5]),
    .in_7(in_1[6]), .in_8(in_1[7]), .out_9(n8bitdd_1_out_9), .out_10(n8bitdd_1_out_10),
    .out_11(n8bitdd_1_out_11));
  main main_1 (
    .A(n8bitdd_1_out_11[3]), .B(n8bitdd_1_out_11[2]), .C(n8bitdd_1_out_11[1]), .D(n8bitdd_1_out_11[0]),
    .out_6(main_1_out_6), .out_5(main_1_out_5), .out_7(main_1_out_7), .out_8(main_1_out_8),
    .out_9(main_1_out_9), .out_10(main_1_out_10), .out_11(main_1_out_11));
  _7_Segment_Display u_7_segment_display_1 (
    .g(main_1_out_8), .f(main_1_out_7), .a(main_1_out_5), .b(main_1_out_6), .e(main_1_out_9),
    .d(main_1_out_10), .c(main_1_out_11));  // open: dp
  main main_2 (
    .A(n8bitdd_1_out_10[3]), .B(n8bitdd_1_out_10[2]), .C(n8bitdd_1_out_10[1]), .D(n8bitdd_1_out_10[0]),
    .out_6(main_2_out_6), .out_5(main_2_out_5), .out_7(main_2_out_7), .out_8(main_2_out_8),
    .out_9(main_2_out_9), .out_10(main_2_out_10), .out_11(main_2_out_11));
  _7_Segment_Display u_7_segment_display_2 (
    .g(main_2_out_8), .f(main_2_out_7), .a(main_2_out_5), .b(main_2_out_6), .e(main_2_out_9),
    .d(main_2_out_10), .c(main_2_out_11));  // open: dp
  main main_3 (
    .A(n8bitdd_1_out_9[3]), .B(n8bitdd_1_out_9[2]), .C(n8bitdd_1_out_9[1]), .D(n8bitdd_1_out_9[0]),
    .out_6(main_3_out_6), .out_5(main_3_out_5), .out_7(main_3_out_7), .out_8(main_3_out_8),
    .out_9(main_3_out_9), .out_10(main_3_out_10), .out_11(main_3_out_11));
  _7_Segment_Display u_7_segment_display_3 (
    .g(main_3_out_8), .f(main_3_out_7), .a(main_3_out_5), .b(main_3_out_6), .e(main_3_out_9),
    .d(main_3_out_10), .c(main_3_out_11));  // open: dp
endmodule

module absoluteValue (
  input  [7:0] in_1,
  input  in_2,
  input  in_3,
  input  in_4,
  input  in_5,
  input  in_6,
  input  in_7,
  input  in_8,
  input  in_9
);

  wire main_1_out_5, main_1_out_6, main_1_out_7, main_1_out_8, main_1_out_9, main_1_out_10, main_1_out_11,
       main_2_out_5, main_2_out_6, main_2_out_7, main_2_out_8, main_2_out_9, main_2_out_10, main_2_out_11,
       main_3_out_5, main_3_out_6, main_3_out_7, main_3_out_8, main_3_out_9, main_3_out_10, main_3_out_11;
  wire [3:0] n8bitdd_1_out_9, n8bitdd_1_out_10, n8bitdd_1_out_11;
  wire [7:0] multiplexer_1_out, subtractor_1_out;

  Multiplexer #(.width(8)) multiplexer_1 (
    .in0({in_2, in_3, in_4, in_5, in_6, in_7, in_8, in_9}), .in1(subtractor_1_out), .out(multiplexer_1_out),
    .sel(in_2));  // open: en
  _8bitDD u_8bitdd_1 (
    .in_1(multiplexer_1_out[0]), .in_2(multiplexer_1_out[1]), .in_3(multiplexer_1_out[2]),
    .in_4(multiplexer_1_out[3]), .in_5(multiplexer_1_out[4]), .in_6(multiplexer_1_out[5]),
    .in_7(multiplexer_1_out[6]), .in_8(multiplexer_1_out[7]), .out_9(n8bitdd_1_out_9),
    .out_10(n8bitdd_1_out_10), .out_11(n8bitdd_1_out_11));
  Subtractor subtractor_1 (
    .a(in_1), .b({in_2, in_3, in_4, in_5, in_6, in_7, in_8, in_9}), .out(subtractor_1_out));  // open: bin, bout
  _7_Segment_Display u_7_segment_display_1 (.g(in_2));  // open: f, a, b, e, d, c, dp
  main main_1 (
    .A(n8bitdd_1_out_11[3]), .B(n8bitdd_1_out_11[2]), .C(n8bitdd_1_out_11[1]), .D(n8bitdd_1_out_11[0]),
    .out_6(main_1_out_6), .out_5(main_1_out_5), .out_7(main_1_out_7), .out_8(main_1_out_8),
    .out_9(main_1_out_9), .out_10(main_1_out_10), .out_11(main_1_out_11));
  _7_Segment_Display u_7_segment_display_2 (
    .g(main_1_out_8), .f(main_1_out_7), .a(main_1_out_5), .b(main_1_out_6), .e(main_1_out_9),
    .d(main_1_out_10), .c(main_1_out_11));  // open: dp
  main main_2 (
    .A(n8bitdd_1_out_10[3]), .B(n8bitdd_1_out_10[2]), .C(n8bitdd_1_out_10[1]), .D(n8bitdd_1_out_10[0]),
    .out_6(main_2_out_6), .out_5(main_2_out_5), .out_7(main_2_out_7), .out_8(main_2_out_8),
    .out_9(main_2_out_9), .out_10(main_2_out_10), .out_11(main_2_out_11));
  _7_Segment_Display u_7_segment_display_3 (
    .g(main_2_out_8), .f(main_2_out_7), .a(main_2_out_5), .b(main_2_out_6), .e(main_2_out_9),
    .d(main_2_out_10), .c(main_2_out_11));  // open: dp
  main main_3 (
    .A(n8bitdd_1_out_9[3]), .B(n8bitdd_1_out_9[2]), .C(n8bitdd_1_out_9[1]), .D(n8bitdd_1_out_9[0]),
    .out_6(main_3_out_6), .out_5(main_3_out_5), .out_7(main_3_out_7), .out_8(main_3_out_8),
    .out_9(main_3_out_9), .out_10(main_3_out_10), .out_11(main_3_out_11));
  _7_Segment_Display u_7_segment_display_4 (
    .g(main_3_out_8), .f(main_3_out_7), .a(main_3_out_5), .b(main_3_out_6), .e(main_3_out_9),
    .d(main_3_out_10), .c(main_3_out_11));  // open: dp
endmodule
